# Fritzing sketch MasterMind-BreadBoard (saved by Fritzing 0.9.1b)
breadboards: 1

parts:
  LCD1 = LCD screen
  S1 = Pushbutton [package="[THT]"]
  S2 = Pushbutton [package="[THT]"]
  S3 = Pushbutton [package="[THT]"]
  S4 = Pushbutton [package="[THT]"]
  R7 = Trimmer Potentiometer [maximum_resistance=10kΩ package=THT]
  Arduino1 = Arduino Uno (Rev3)

nets:
  VSS: LCD1.VSS, LCD1.R/W, S1.Pin_1, S1.Pin_2, S2.Pin_1, S2.Pin_2, S3.Pin_1, S3.Pin_2, S4.Pin_1, S4.Pin_2, R7.leg1, Arduino1.GND
  VDD: LCD1.VDD, R7.leg2, Arduino1.5V
  N1: LCD1.V0, R7.wiper
  N2: LCD1.RS, Arduino1.D2
  N3: LCD1.E, Arduino1.D3_PWM
  N4: LCD1.DB4, Arduino1.D4
  N5: LCD1.DB5, Arduino1.D5_PWM
  N6: LCD1.DB6, Arduino1.D6_PWM
  N7: LCD1.DB7, Arduino1.D7
  N8: S1.Pin_3, S1.Pin_4, Arduino1.D9_PWM
  N9: S2.Pin_3, S2.Pin_4, Arduino1.D10_PWM/SS
  N10: S3.Pin_3, S3.Pin_4, Arduino1.D11_PWM/MOSI
  N11: S4.Pin_3, S4.Pin_4, Arduino1.D12/MISO
